// Logisim project Circuit.circ as structural Verilog: 2 circuits, main circuit main
module main (
  input  [3:0] Multiplier,
  input  Start,
  input  [3:0] Multiplicand,
  input  Reset,
  output Ready
);

  wire adder_1_cout, and_1_out, C__Carry_out, Clock_out, Controller_add_register, Controller_increase_p,
       Controller_load_register, Controller_shift_register;
  wire [1:0] P__Counter_q;
  wire [3:0] A__Sum_q3, adder_1_out, B__Mutiplicand_q3, Bin_to_BCD_p3, Bin_to_BCD_p4, Bin_to_BCD_p5,
       Q__Multiplier_q3;

  Shift_Register #(.length(1)) C__Carry (
    .shift(Controller_shift_register), .in(1'b0), .clk(Clock_out), .out(C__Carry_out),
    .load(Controller_add_register), .clr(Reset), .d0(adder_1_cout));  // open: q0
  Clock Clock (.out(Clock_out));
  Shift_Register #(.length(4)) A__Sum (
    .shift(Controller_shift_register), .in(C__Carry_out), .clk(Clock_out), .load(Controller_add_register),
    .clr(Reset), .d0(adder_1_out[3]), .q0(A__Sum_q3[3]), .d1(adder_1_out[2]), .q1(A__Sum_q3[2]),
    .d2(adder_1_out[1]), .q2(A__Sum_q3[1]), .d3(adder_1_out[0]), .q3(A__Sum_q3[0]));  // open: out
  Shift_Register #(.length(4)) B__Mutiplicand (
    .shift(1'b0), .clk(Clock_out), .load(Controller_load_register), .clr(Reset), .d0(Multiplicand[3]),
    .q0(B__Mutiplicand_q3[3]), .d1(Multiplicand[2]), .q1(B__Mutiplicand_q3[2]), .d2(Multiplicand[1]),
    .q2(B__Mutiplicand_q3[1]), .d3(Multiplicand[0]), .q3(B__Mutiplicand_q3[0]));  // open: in, out
  Shift_Register #(.length(4)) Q__Multiplier (
    .shift(Controller_shift_register), .in(A__Sum_q3[0]), .clk(Clock_out), .load(Controller_load_register),
    .clr(Reset), .d0(Multiplier[3]), .q0(Q__Multiplier_q3[3]), .d1(Multiplier[2]), .q1(Q__Multiplier_q3[2]),
    .d2(Multiplier[1]), .q2(Q__Multiplier_q3[1]), .d3(Multiplier[0]), .q3(Q__Multiplier_q3[0]));  // open: out
  Adder #(.width(4)) adder_1 (
    .a(A__Sum_q3), .b(B__Mutiplicand_q3), .out(adder_1_out), .cout(adder_1_cout));  // open: cin
  Counter #(.width(2), .max('h3)) P__Counter (
    .load(1'b0), .count(Controller_increase_p), .Q(P__Counter_q), .clk(Clock_out),
    .clr(Controller_load_register));  // open: D, carry
  and and_1 (and_1_out, P__Counter_q[0], P__Counter_q[1]);
  Controller Controller (
    .Start(Start), .Q_0(Q__Multiplier_q3[0]), .Zero(and_1_out), .Clock(Clock_out), .Reset(Reset),
    .Ready(Ready), .Load_Register(Controller_load_register), .Add_Register(Controller_add_register),
    .Increase_P(Controller_increase_p), .Shift_register(Controller_shift_register));
  // Binary_to_BCD_8x12 Bin_to_BCD: pin names not known; wires that end beside it: {A__Sum_q3, Q__Multiplier_q3}, 1'b0, Bin_to_BCD_p3, Bin_to_BCD_p4, Bin_to_BCD_p5
  Hex_Digit_Display hex_digit_display_1 (.value(Bin_to_BCD_p3));  // open: dp
  Hex_Digit_Display hex_digit_display_2 (.value(Bin_to_BCD_p4));  // open: dp
  Hex_Digit_Display hex_digit_display_3 (.value(Bin_to_BCD_p5));  // open: dp
endmodule

module Controller (
  input  Start,
  input  Q_0,
  input  Zero,
  input  Clock,
  input  Reset,
  output Ready,
  output Load_Register,
  output Add_Register,
  output Increase_P,
  output Shift_register
);

  wire and_1_out, and_2_out, and_3_out, and_4_out, not_1_out, not_2_out, or_1_out, or_2_out, S_Add_q;

  not not_1 (not_1_out, Start);
  not not_2 (not_2_out, Zero);
  and and_1 (and_1_out, Ready, not_1_out);
  and and_2 (and_2_out, Zero, Increase_P);
  and and_3 (and_3_out, Start, Ready);
  and and_4 (and_4_out, not_2_out, Increase_P);
  or or_1 (or_1_out, and_1_out, and_2_out);
  or or_2 (or_2_out, and_3_out, and_4_out);
  D_Flip_Flop S_Idle (.clk(Clock), .D(or_1_out), .Q(Ready), .preset(Reset));  // open: Qn, en, reset
  D_Flip_Flop S_Add (.clk(Clock), .D(or_2_out), .Q(S_Add_q), .reset(Reset));  // open: Qn, preset, en
  D_Flip_Flop S_Shift (.clk(Clock), .D(S_Add_q), .Q(Increase_P), .reset(Reset));  // open: Qn, preset, en
  and and_5 (Load_Register, Ready, Start);
  and and_6 (Add_Register, Q_0, S_Add_q);

  assign Shift_register = Increase_P;
endmodule
